# Fritzing sketch HW2 (saved by Fritzing 0.9.3b)
breadboards: 1

parts:
  S1 = Pushbutton [package="[THT]"]
  S2 = Pushbutton [package="[THT]"]
  S3 = Pushbutton [package="[THT]"]
  S4 = Pushbutton [package="[THT]"]
  Part1 = Arduino Uno (Rev3)
  R2 = Resistor [tolerance=±5% resistance=220 package=THT]
  R3 = Resistor [tolerance=±5% resistance=220 package=THT]
  R4 = Resistor [tolerance=±5% resistance=220 package=THT]
  R1 = Resistor [tolerance=±5% resistance=220 package=THT]

nets:
  N1: S1.Pin_1, S1.Pin_2, S2.Pin_1, S2.Pin_2, S3.Pin_1, S3.Pin_2, S4.Pin_1, S4.Pin_2, Part1.GND
  N2: S1.Pin_3, S1.Pin_4, Part1.D7, R1.Pin_0
  N3: S2.Pin_3, S2.Pin_4, Part1.D6_PWM, R2.Pin_0
  N4: S3.Pin_3, S3.Pin_4, Part1.D5_PWM, R3.Pin_0
  N5: S4.Pin_3, S4.Pin_4, Part1.D4, R4.Pin_0
  N6: Part1.3V3, R2.Pin_1, R3.Pin_1, R4.Pin_1, R1.Pin_1
